// Logisim project protection_circuit.circ as structural Verilog: 1 circuit, main circuit main
module main (
);

  wire and_1_out, and_2_out, and_3_out, and_4_out, and_5_out, and_6_out, and_7_out, and_8_out, and_9_out,
       and_10_out, and_11_out, and_12_out, and_13_out, and_14_out, and_15_out, and_16_out, and_17_out,
       and_18_out, and_19_out, and_20_out, and_21_out, and_22_out, and_23_out, and_24_out, and_25_out,
       and_26_out, and_27_out, and_28_out, and_29_out, and_30_out, and_31_out, and_32_out, and_33_out,
       and_34_out, and_35_out, and_36_out, and_37_out, and_38_out, and_39_out, and_40_out, and_41_out,
       and_42_out, and_43_out, buffer_1_out, buffer_2_out, buffer_3_out, buffer_4_out, buffer_6_out,
       buffer_7_out, buffer_8_out, buffer_9_out, buffer_10_out, buffer_11_out, buffer_12_out, buffer_13_out,
       buffer_14_out, buffer_15_out, buffer_16_out, buffer_17_out, buffer_18_out, buffer_19_out,
       controlled_buffer_1_out, controlled_buffer_2_out, controlled_buffer_3_out, controlled_buffer_4_out,
       controlled_buffer_5_out, controlled_buffer_6_out, controlled_buffer_7_out, controlled_buffer_8_out,
       controlled_inverter_1_out, controlled_inverter_2_out, controlled_inverter_3_out,
       controlled_inverter_4_out, controlled_inverter_5_out, controlled_inverter_6_out,
       controlled_inverter_7_out, controlled_inverter_8_out, controlled_inverter_9_out, even_parity_1_out,
       even_parity_2_out, even_parity_3_out, even_parity_4_out, nand_1_out, nand_2_out, nand_3_out,
       nand_4_out, nand_5_out, nand_6_out, nand_7_out, nand_8_out, nand_9_out, nand_10_out, nand_11_out,
       nand_12_out, nand_13_out, nand_14_out, nand_15_out, nand_16_out, nand_17_out, nand_18_out,
       nand_19_out, nand_20_out, nand_21_out, nor_1_out, nor_2_out, nor_3_out, nor_4_out, nor_5_out,
       nor_6_out, nor_7_out, nor_8_out, nor_9_out, nor_10_out, not_1_out, not_2_out, not_3_out, not_4_out,
       not_5_out, not_6_out, not_7_out, not_8_out, not_9_out, not_10_out, not_11_out, not_12_out, not_13_out,
       not_14_out, not_15_out, not_16_out, not_17_out, not_18_out, not_19_out, not_20_out, not_21_out,
       not_22_out, not_23_out, not_24_out, not_25_out, not_26_out, not_27_out, not_28_out, not_29_out,
       not_30_out, not_31_out, not_32_out, not_33_out, not_34_out, not_35_out, not_36_out, not_37_out,
       not_38_out, not_39_out, not_40_out, not_41_out, not_42_out, not_43_out, not_44_out, not_45_out,
       not_46_out, not_47_out, not_48_out, not_49_out, not_50_out, not_51_out, not_52_out, odd_parity_1_out,
       odd_parity_2_out, odd_parity_3_out, odd_parity_4_out, odd_parity_5_out, odd_parity_6_out,
       odd_parity_7_out, odd_parity_8_out, or_1_out, or_2_out, or_3_out, or_4_out, or_5_out, or_6_out,
       or_7_out, or_8_out, or_9_out, or_10_out, or_11_out, or_12_out, or_13_out, or_14_out, or_15_out,
       or_16_out, or_17_out, or_18_out, or_19_out, or_20_out, or_21_out, or_22_out, or_23_out, or_24_out,
       or_25_out, or_26_out, or_27_out, or_28_out, undriven, undriven_2, undriven_3, undriven_4, undriven_5,
       undriven_6, undriven_7, undriven_8, undriven_9, undriven_10, undriven_11, undriven_12, undriven_13,
       undriven_14, undriven_15, undriven_16, undriven_17, undriven_18, undriven_19, xnor_1_out, xnor_2_out,
       xnor_3_out, xnor_4_out, xnor_5_out, xnor_6_out, xnor_7_out, xnor_8_out, xnor_9_out, xnor_10_out,
       xnor_11_out, xnor_12_out, xnor_13_out, xnor_14_out, xnor_15_out, xnor_16_out, xnor_17_out, xor_1_out,
       xor_2_out, xor_3_out, xor_4_out, xor_5_out, xor_6_out, xor_7_out, xor_8_out, xor_9_out, xor_10_out,
       xor_11_out, xor_12_out, xor_13_out, xor_14_out, xor_15_out, xor_16_out, xor_17_out, xor_18_out,
       xor_19_out, xor_20_out, xor_21_out, xor_22_out, xor_23_out, xor_24_out, xor_25_out, xor_26_out,
       xor_27_out, xor_28_out, xor_29_out, xor_30_out, xor_31_out, xor_32_out, xor_33_out, xor_34_out,
       xor_35_out, xor_36_out;

  not not_1 (not_1_out, undriven_14);
  xor xor_1 (xor_1_out, undriven, undriven_2);
  or or_1 (or_1_out, undriven_2, not_1_out);
  buf buffer_1 (buffer_1_out, undriven);
  not not_2 (not_2_out, undriven_15);
  and and_1 (and_1_out, undriven_15, undriven_13);
  nor nor_1 (nor_1_out, undriven_13, undriven_3);
  xor xor_2 (xor_2_out, undriven_4, undriven_4);
  // Probe on xnor_1_out
  xnor xnor_1 (xnor_1_out, undriven_4, undriven_5);
  // Probe on xor_1_out
  // Probe on or_1_out
  // Probe on buffer_1_out
  // Probe on not_2_out
  // Probe on and_1_out
  // Probe on nor_1_out
  // Probe on xor_2_out
  // Probe on buffer_2_out
  buf buffer_2 (buffer_2_out, xor_1_out);
  and and_2 (and_2_out, 1'b0, undriven_10);
  not not_3 (not_3_out, undriven_11);
  // Probe on xor_3_out
  xor xor_3 (xor_3_out, or_1_out, buffer_1_out);
  or or_2 (or_2_out, undriven_11, undriven_12);
  // Probe on and_3_out
  and and_3 (and_3_out, buffer_1_out, undriven_16);
  // Probe on xor_4_out
  xor xor_4 (xor_4_out, undriven_17, and_1_out);
  // Probe on not_4_out
  not not_4 (not_4_out, and_1_out);
  not not_5 (not_5_out, and_5_out);
  // Probe on nand_1_out
  nand nand_1 (nand_1_out, nor_1_out, xor_2_out);
  // Probe on xor_5_out
  xor xor_5 (xor_5_out, xor_2_out, xnor_1_out);
  xnor xnor_2 (xnor_2_out, undriven_6, undriven_7);
  and and_4 (and_4_out, undriven_8, undriven_9);
  // Probe on buffer_3_out
  buf buffer_3 (buffer_3_out, xnor_1_out);
  and and_5 (and_5_out, not_5_out, not_5_out);
  or or_3 (or_3_out, xnor_2_out, and_4_out);
  nand nand_2 (nand_2_out, 1'b0, undriven_10);
  xor xor_6 (xor_6_out, and_2_out, not_3_out);
  // Probe on odd_parity_1_out
  xor odd_parity_1 (odd_parity_1_out, buffer_2_out, undriven_19);
  // Probe on and_6_out
  and and_6 (and_6_out, xor_3_out, xor_4_out);
  // Probe on nor_2_out
  not nor_2 (nor_2_out, nand_1_out);  // NOR_Gate
  not xnor_3 (xnor_3_out, xor_4_out);  // XNOR_Gate
  nand nand_3 (nand_3_out, xor_4_out, nand_1_out);
  // Probe on xnor_4_out
  xnor xnor_4 (xnor_4_out, nand_1_out, xor_5_out);
  // Probe on nand_4_out
  nand nand_4 (nand_4_out, undriven_18, nand_1_out);
  nand nand_5 (nand_5_out, xnor_2_out, or_3_out);
  // Probe on xor_7_out
  xor xor_7 (xor_7_out, undriven_18, buffer_3_out);
  // Probe on xnor_3_out
  // Probe on nand_3_out
  and and_7 (and_7_out, odd_parity_1_out, buffer_2_out);
  or or_4 (or_4_out, xor_6_out, or_2_out);
  or or_5 (or_5_out, and_6_out, and_6_out);
  nor nor_3 (nor_3_out, nor_2_out, xnor_3_out);
  or or_6 (or_6_out, nand_4_out, nand_4_out);
  // Probe on and_7_out
  xnor xnor_5 (xnor_5_out, nand_2_out, or_4_out);
  // Probe on or_5_out
  // Probe on nor_3_out
  // Probe on xnor_6_out
  xnor xnor_6 (xnor_6_out, xnor_3_out, not_4_out);
  // Probe on nand_6_out
  nand nand_6 (nand_6_out, nand_3_out, xnor_4_out);
  // Probe on xnor_7_out
  xnor xnor_7 (xnor_7_out, xnor_4_out, nand_4_out);
  // Probe on or_6_out
  // Probe on or_7_out
  or or_7 (or_7_out, nand_4_out, xor_7_out);
  or or_8 (or_8_out, nand_5_out, nand_5_out);
  and and_8 (and_8_out, nand_2_out, xnor_5_out, or_4_out, or_2_out);
  not not_6 (not_6_out, xnor_6_out);
  xor xor_8 (xor_8_out, xnor_6_out, nand_6_out);
  buf buffer_4 (buffer_4_out, and_7_out);
  not not_7 (not_7_out, and_8_out);
  buf buffer_5 (not_7_out, and_8_out);
  assign controlled_buffer_1_out = or_5_out ? or_5_out : 1'bz;  // Controlled_Buffer controlled_buffer_1
  assign controlled_buffer_2_out = nor_3_out ? nor_3_out : 1'bz;  // Controlled_Buffer controlled_buffer_2
  assign controlled_inverter_1_out = or_6_out ? ~xnor_7_out : 1'bz;  // Controlled_Inverter controlled_inverter_1
  not not_8 (not_8_out, or_7_out);
  buf buffer_6 (buffer_6_out, buffer_4_out);
  not not_9 (not_9_out, or_7_out);
  not not_10 (not_10_out, not_8_out);
  assign controlled_buffer_3_out = not_11_out ? and_7_out : 1'bz;  // Controlled_Buffer controlled_buffer_3
  not not_11 (not_11_out, buffer_6_out);
  and and_9 (and_9_out, controlled_buffer_1_out, or_5_out, controlled_buffer_2_out);
  not not_12 (not_12_out, not_10_out);
  not not_13 (not_13_out, not_12_out);
  // Probe on controlled_buffer_3_out
  // Probe on and_9_out
  // Probe on and_10_out
  and and_10 (and_10_out, xnor_6_out, not_6_out, xor_8_out, nand_6_out);
  // Probe on buffer_7_out
  buf buffer_7 (buffer_7_out, xnor_7_out);
  // Probe on and_11_out
  and and_11 (and_11_out, controlled_inverter_1_out, or_6_out);
  // Probe on xor_9_out
  xor xor_9 (xor_9_out, or_6_out, not_9_out);
  // Probe on odd_parity_2_out
  xor odd_parity_2 (odd_parity_2_out, not_9_out, xnor_7_out);
  // Probe on not_14_out
  not not_14 (not_14_out, not_13_out);
  not not_15 (not_15_out, 1'b1);
  not not_16 (not_16_out, 1'b0);
  not not_17 (not_17_out, and_10_out);
  not not_18 (not_18_out, buffer_7_out);
  not not_19 (not_19_out, not_15_out);
  and and_12 (and_12_out, not_15_out, not_16_out);
  or or_9 (or_9_out, not_16_out, not_19_out);
  // Probe on xnor_8_out
  xnor xnor_8 (xnor_8_out, controlled_buffer_3_out, and_9_out);
  // Probe on nand_7_out
  nand nand_7 (nand_7_out, and_9_out, and_9_out);
  // Probe on xnor_9_out
  NotExactlyOne xnor_9 (.out(xnor_9_out), .in0(and_9_out), .in1(and_9_out), .in2(and_10_out));
  // Probe on and_13_out
  and and_13 (and_13_out, not_17_out, and_9_out, not_18_out, and_11_out);
  // Probe on nor_4_out
  nor nor_4 (nor_4_out, buffer_7_out, and_11_out);
  and and_14 (and_14_out, buffer_7_out, and_11_out);
  xor xor_10 (xor_10_out, and_11_out, xor_9_out);
  xor xor_11 (xor_11_out, odd_parity_2_out, not_14_out);
  nand nand_8 (nand_8_out, and_12_out, or_9_out);
  and and_15 (and_15_out, or_9_out, or_9_out, and_12_out, not_15_out);
  // Probe on and_14_out
  // Probe on xor_10_out
  // Probe on xor_11_out
  not not_20 (not_20_out, nand_8_out);
  not not_21 (not_21_out, xor_10_out);
  not not_22 (not_22_out, not_21_out);
  nand nand_9 (nand_9_out, not_20_out, and_15_out);
  not not_23 (not_23_out, not_22_out);
  not not_24 (not_24_out, xor_11_out);
  // Probe on and_16_out
  and and_16 (and_16_out, xnor_8_out, and_9_out);
  or or_10 (or_10_out, nand_7_out, xnor_9_out);
  // Probe on nand_10_out
  nand nand_10 (nand_10_out, and_13_out, nor_4_out);
  or or_11 (or_11_out, and_14_out, xor_10_out);
  // Probe on not_25_out
  not not_25 (not_25_out, not_23_out);
  nor nor_5 (nor_5_out, xor_10_out, xor_11_out);
  and and_17 (and_17_out, not_21_out, not_24_out);
  // Probe on or_10_out
  // Probe on xnor_10_out
  xnor xnor_10 (xnor_10_out, xnor_9_out, and_13_out);
  // Probe on or_11_out
  // Probe on nor_5_out
  // Probe on and_17_out
  buf buffer_8 (buffer_8_out, and_16_out);
  buf buffer_9 (buffer_9_out, buffer_8_out);
  buf buffer_10 (buffer_10_out, buffer_9_out);
  not not_26 (not_26_out, buffer_8_out);
  or or_12 (or_12_out, and_16_out, buffer_10_out);
  and and_18 (and_18_out, not_26_out, or_10_out);
  or or_13 (or_13_out, or_10_out, xnor_10_out);
  // Probe on or_12_out
  // Probe on and_18_out
  // Probe on or_13_out
  // Probe on xor_12_out
  xor xor_12 (xor_12_out, 1'b0, nand_10_out);
  // Probe on and_19_out
  and and_19 (and_19_out, or_11_out, not_25_out, nand_10_out);
  // Probe on xnor_11_out
  xnor xnor_11 (xnor_11_out, not_25_out, xor_10_out);
  // Probe on nand_11_out
  nand nand_11 (nand_11_out, nor_5_out, and_17_out);
  // Probe on xor_13_out
  xor xor_13 (xor_13_out, and_17_out, and_17_out);
  ExactlyOne xor_14 (
    .out(xor_14_out), .in0(or_12_out), .in1(or_12_out), .in2(or_12_out), .in3(or_12_out), .in4(or_12_out));
  assign controlled_inverter_2_out = or_13_out ? ~and_18_out : 1'bz;  // Controlled_Inverter controlled_inverter_2
  assign controlled_inverter_3_out = and_18_out ? ~or_13_out : 1'bz;  // Controlled_Inverter controlled_inverter_3
  not not_27 (not_27_out, xor_13_out);
  // Probe on buffer_11_out
  buf buffer_11 (buffer_11_out, xor_14_out);
  // Probe on nand_12_out
  nand nand_12 (nand_12_out, controlled_inverter_2_out, controlled_inverter_3_out);
  // Probe on and_20_out
  and and_20 (and_20_out, and_19_out, xor_12_out);
  // Probe on xor_15_out
  xor xor_15 (xor_15_out, xor_12_out, and_19_out);
  // Probe on xor_16_out
  xor xor_16 (xor_16_out, and_19_out, xnor_11_out);
  // Probe on or_14_out
  or or_14 (or_14_out, 1'b0, 1'b0, 1'b0, 1'b0, xnor_11_out);
  nor nor_6 (nor_6_out, 1'b0, nand_11_out);
  // Probe on and_21_out
  and and_21 (and_21_out, not_27_out, not_27_out);
  // Probe on nor_6_out
  not not_28 (not_28_out, and_20_out);
  xnor xnor_12 (xnor_12_out, buffer_11_out, buffer_11_out);
  // Probe on controlled_buffer_4_out
  assign controlled_buffer_4_out = xnor_12_out ? buffer_11_out : 1'bz;  // Controlled_Buffer controlled_buffer_4
  and and_22 (and_22_out, buffer_11_out, xnor_12_out, nand_12_out);
  and and_23 (and_23_out, nand_12_out, not_28_out, xor_15_out);
  or or_15 (or_15_out, and_20_out, xor_15_out, xor_15_out);
  nand nand_13 (nand_13_out, xor_16_out, or_14_out, and_20_out, and_20_out);
  // Probe on and_22_out
  // Probe on and_23_out
  // Probe on or_15_out
  // Probe on not_29_out
  not not_29 (not_29_out, nand_13_out);
  // Probe on not_30_out
  not not_30 (not_30_out, nand_13_out);
  // Probe on xor_17_out
  xor xor_17 (xor_17_out, nor_6_out, 1'b1);
  // Probe on and_24_out
  and and_24 (and_24_out, and_21_out, 1'b1);
  not not_31 (not_31_out, not_30_out);
  not not_32 (not_32_out, xor_17_out);
  // Probe on buffer_12_out
  buf buffer_12 (buffer_12_out, controlled_buffer_4_out);
  xnor xnor_13 (xnor_13_out, controlled_buffer_4_out, and_22_out);
  // Probe on xor_18_out
  xor xor_18 (xor_18_out, and_22_out, and_23_out);
  nor nor_7 (nor_7_out, and_23_out, or_15_out);
  xor xor_19 (xor_19_out, or_15_out, not_29_out);
  nand nand_14 (nand_14_out, not_29_out, not_30_out);
  and and_25 (and_25_out, not_31_out, not_32_out);
  // Probe on xnor_13_out
  // Probe on nor_7_out
  // Probe on xor_19_out
  // Probe on nand_14_out
  // Probe on and_25_out
  // Probe on xnor_14_out
  xnor xnor_14 (xnor_14_out, xor_17_out, and_24_out);
  assign controlled_inverter_4_out = xnor_13_out ? ~buffer_12_out : 1'bz;  // Controlled_Inverter controlled_inverter_4
  or or_16 (or_16_out, controlled_inverter_4_out, buffer_12_out);
  // Probe on and_26_out
  and and_26 (and_26_out, or_16_out, buffer_12_out);
  // Probe on buffer_13_out
  buf buffer_13 (buffer_13_out, xnor_13_out);
  // Probe on odd_parity_3_out
  xor odd_parity_3 (odd_parity_3_out, xor_18_out, xor_18_out);
  nand nand_15 (nand_15_out, xor_18_out, nor_7_out);
  ExactlyOne xor_20 (.out(xor_20_out), .in0(nor_7_out), .in1(nor_7_out), .in2(xor_19_out));
  xnor even_parity_1 (even_parity_1_out, xor_19_out, nor_7_out, nand_14_out, not_29_out);
  // Probe on or_17_out
  or or_17 (or_17_out, nand_14_out, and_25_out);
  xor xor_21 (xor_21_out, and_25_out, xnor_14_out);
  // Probe on nand_15_out
  // Probe on xor_20_out
  // Probe on even_parity_1_out
  // Probe on xor_21_out
  xnor even_parity_2 (even_parity_2_out, and_26_out, 1'b1);
  not not_33 (not_33_out, buffer_13_out);
  xor xor_22 (xor_22_out, xor_20_out, xor_20_out);
  and and_27 (and_27_out, xor_20_out, even_parity_1_out, xor_21_out);
  or or_18 (or_18_out, xor_21_out, or_17_out);
  and and_28 (and_28_out, or_17_out, xor_21_out);
  // Probe on even_parity_2_out
  // Probe on not_33_out
  // Probe on nand_16_out
  nand nand_16 (nand_16_out, odd_parity_3_out, odd_parity_3_out);
  // Probe on or_19_out
  or or_19 (or_19_out, odd_parity_3_out, nand_15_out, xor_20_out);
  // Probe on xor_22_out
  // Probe on and_27_out
  // Probe on or_18_out
  // Probe on and_28_out
  not not_34 (not_34_out, not_33_out);
  not not_35 (not_35_out, even_parity_2_out);
  and and_29 (and_29_out, and_27_out, xor_21_out);
  not not_36 (not_36_out, not_35_out);
  not not_37 (not_37_out, and_29_out);
  not not_38 (not_38_out, not_36_out);
  not not_39 (not_39_out, not_38_out);
  // Probe on xor_23_out
  xor xor_23 (xor_23_out, not_36_out, not_39_out);
  // Probe on or_20_out
  or or_20 (or_20_out, not_33_out, not_34_out);
  // Probe on and_30_out
  and and_30 (and_30_out, buffer_13_out, nand_16_out);
  xnor xnor_15 (xnor_15_out, or_19_out, not_33_out);
  // Probe on xor_24_out
  xor xor_24 (xor_24_out, xor_22_out, and_27_out);
  // Probe on buffer_14_out
  buf buffer_14 (buffer_14_out, not_37_out);
  // Probe on even_parity_3_out
  xnor even_parity_3 (even_parity_3_out, or_18_out, xor_21_out, and_27_out, xor_21_out, and_27_out);
  nor nor_8 (nor_8_out, and_28_out, and_28_out);
  // Probe on xnor_15_out
  // Probe on nor_8_out
  or or_21 (or_21_out, xor_23_out, xor_23_out);
  // Probe on controlled_inverter_5_out
  assign controlled_inverter_5_out = and_30_out ? ~or_20_out : 1'bz;  // Controlled_Inverter controlled_inverter_5
  // Probe on controlled_buffer_5_out
  assign controlled_buffer_5_out = or_20_out ? and_30_out : 1'bz;  // Controlled_Buffer controlled_buffer_5
  // Probe on or_21_out
  // Probe on or_22_out
  or or_22 (or_22_out, nand_16_out, xnor_15_out, xor_24_out, or_20_out);
  // Probe on nand_17_out
  nand nand_17 (nand_17_out, xor_24_out, and_30_out);
  // Probe on xor_25_out
  xor xor_25 (xor_25_out, buffer_14_out, even_parity_3_out);
  // Probe on odd_parity_4_out
  xor odd_parity_4 (odd_parity_4_out, even_parity_3_out, and_27_out);
  // Probe on xor_26_out
  xor xor_26 (xor_26_out, nor_8_out, 1'b1);
  xor odd_parity_5 (odd_parity_5_out, or_22_out, nand_17_out);
  xnor even_parity_4 (even_parity_4_out, nand_17_out, nand_17_out);
  assign controlled_inverter_6_out = xor_26_out ? ~xor_26_out : 1'bz;  // Controlled_Inverter controlled_inverter_6
  and and_31 (and_31_out, or_21_out, controlled_inverter_5_out);
  not not_40 (not_40_out, and_31_out);
  // Probe on controlled_buffer_6_out
  assign controlled_buffer_6_out = not_40_out ? or_21_out : 1'bz;  // Controlled_Buffer controlled_buffer_6
  xor xor_27 (xor_27_out, controlled_inverter_5_out, controlled_buffer_5_out);
  xor xor_28 (xor_28_out, controlled_buffer_5_out, or_22_out);
  and and_32 (and_32_out, odd_parity_5_out, even_parity_4_out);
  // Probe on xor_27_out
  // Probe on xor_28_out
  // Probe on and_32_out
  // Probe on or_23_out
  or or_23 (or_23_out, nand_17_out, even_parity_4_out);
  // Probe on nand_18_out
  nand nand_18 (nand_18_out, xor_25_out, odd_parity_4_out);
  // Probe on odd_parity_6_out
  xor odd_parity_6 (odd_parity_6_out, odd_parity_4_out, odd_parity_4_out, odd_parity_4_out);
  // Probe on xor_29_out
  xor xor_29 (xor_29_out, odd_parity_4_out, controlled_inverter_6_out);
  assign controlled_inverter_7_out = xor_27_out ? ~controlled_buffer_6_out : 1'bz;  // Controlled_Inverter controlled_inverter_7
  assign controlled_inverter_8_out = xor_27_out ? ~controlled_inverter_7_out : 1'bz;  // Controlled_Inverter controlled_inverter_8
  assign controlled_inverter_9_out = or_23_out ? ~and_32_out : 1'bz;  // Controlled_Inverter controlled_inverter_9
  assign controlled_buffer_7_out = and_32_out ? or_23_out : 1'bz;  // Controlled_Buffer controlled_buffer_7
  and and_33 (and_33_out, xor_27_out, and_32_out);
  // Probe on xor_30_out
  xor xor_30 (xor_30_out, controlled_buffer_6_out, controlled_inverter_8_out);
  // Probe on and_34_out
  and and_34 (and_34_out, xor_27_out, and_33_out);
  xor xor_31 (xor_31_out, xor_28_out, and_32_out);
  nor nor_9 (nor_9_out, controlled_inverter_9_out, controlled_buffer_7_out);
  nand nand_19 (nand_19_out, or_23_out, nand_18_out);
  xnor xnor_16 (xnor_16_out, nand_18_out, odd_parity_6_out);
  // Probe on and_35_out
  and and_35 (and_35_out, odd_parity_6_out, nand_18_out);
  // Probe on controlled_buffer_8_out
  assign controlled_buffer_8_out = xor_29_out ? xor_29_out : 1'bz;  // Controlled_Buffer controlled_buffer_8
  // Probe on xor_31_out
  // Probe on nor_9_out
  // Probe on nand_19_out
  // Probe on xnor_16_out
  not not_41 (not_41_out, and_34_out);
  not not_42 (not_42_out, xnor_16_out);
  not not_43 (not_43_out, nor_9_out);
  // Probe on or_24_out
  or or_24 (or_24_out, xor_30_out, not_41_out);
  // Probe on xor_32_out
  xor xor_32 (xor_32_out, and_34_out, and_33_out);
  // Probe on xnor_17_out
  xnor xnor_17 (xnor_17_out, xor_31_out, not_43_out);
  // Probe on or_25_out
  or or_25 (or_25_out, nor_9_out, controlled_buffer_7_out);
  // Probe on or_26_out
  or or_26 (or_26_out, nand_19_out, not_42_out);
  // Probe on and_36_out
  and and_36 (and_36_out, xnor_16_out, odd_parity_6_out);
  // Probe on odd_parity_7_out
  xor odd_parity_7 (odd_parity_7_out, and_35_out, controlled_buffer_8_out);
  // Probe on odd_parity_8_out
  xor odd_parity_8 (odd_parity_8_out, and_35_out, controlled_buffer_8_out);
  not not_44 (not_44_out, or_26_out);
  // Probe on and_37_out
  and and_37 (and_37_out, or_24_out, or_24_out);
  // Probe on xor_33_out
  xor xor_33 (xor_33_out, xor_32_out, and_33_out);
  // Probe on xor_34_out
  xor xor_34 (xor_34_out, xnor_17_out, nor_9_out);
  // Probe on and_38_out
  and and_38 (and_38_out, or_25_out, not_44_out);
  // Probe on and_39_out
  and and_39 (and_39_out, 1'b1, or_26_out);
  // Probe on buffer_15_out
  buf buffer_15 (buffer_15_out, and_36_out);
  or or_27 (or_27_out, odd_parity_7_out, odd_parity_8_out);
  // Probe on and_40_out
  and and_40 (and_40_out, odd_parity_7_out, odd_parity_8_out);
  // Probe on or_27_out
  not not_45 (not_45_out, and_37_out);
  not not_46 (not_46_out, and_37_out);
  nand nand_20 (nand_20_out, not_45_out, not_46_out);
  and and_41 (and_41_out, and_37_out, xor_34_out, xor_33_out);
  // XOR_Gate xor_35 has open pins: out=xor_35_out
  // Probe on or_28_out
  or or_28 (or_28_out, and_38_out, nor_9_out);
  // Probe on and_42_out
  and and_42 (and_42_out, and_39_out, 1'b0);
  // Probe on nor_10_out
  nor nor_10 (nor_10_out, buffer_15_out, buffer_15_out);
  // Probe on xor_36_out
  buf xor_36 (xor_36_out, or_27_out);  // XOR_Gate
  nand nand_21 (nand_21_out, or_27_out, and_40_out);
  // Probe on nand_20_out
  // Probe on and_41_out
  // Probe on xor_35_out
  // Probe on nand_21_out
  buf buffer_16 (buffer_16_out, nand_20_out);
  not not_47 (not_47_out, and_41_out);
  buf buffer_17 (buffer_17_out, xor_35_out);
  buf buffer_18 (buffer_18_out, or_28_out);
  buf buffer_19 (buffer_19_out, nand_21_out);
  // Probe on buffer_16_out
  // Probe on not_47_out
  // Probe on buffer_17_out
  // Probe on buffer_18_out
  // Probe on not_48_out
  not not_48 (not_48_out, and_42_out);
  // Probe on not_49_out
  not not_49 (not_49_out, nor_10_out);
  // Probe on not_50_out
  not not_50 (not_50_out, xor_36_out);
  // Probe on buffer_19_out
  not not_51 (not_51_out, buffer_16_out);
  not not_52 (not_52_out, not_50_out);
  and and_43 (and_43_out, not_51_out, not_47_out, buffer_17_out, buffer_18_out, not_48_out, not_49_out, not_52_out, buffer_19_out);
  LED led_1 (.in(and_43_out));
  // also tied to GND on the sheet: {or_8_out, nand_9_out}
endmodule
